// Logisim project 441_cache.circ as structural Verilog: 1 circuit, main circuit main
module main (
  input  [7:0] in_1,
  input  [7:0] in_2,
  input  [7:0] in_3
);

  wire button_2_out, button_3_out, button_4_out, button_5_out, CLOCK, comparator_1_eq, comparator_2_eq,
       comparator_3_eq, comparator_4_eq, or_1_out, R;
  wire [7:0] controlled_buffer_1_out, get_biggest_1_out_9, register_1_q, register_2_q, register_3_q,
       register_4_q, register_5_q, register_6_q, register_7_q, register_8_q;

  Button button_1 (.out(CLOCK));
  Button reset (.out(R));
  Register register_1 (.D(in_2), .en(1'b1), .Q(register_1_q), .clr(R));  // open: clk
  Register register_2 (.D(in_2), .en(1'b1), .Q(register_2_q), .clr(R));  // open: clk
  Register register_3 (.D(in_2), .en(1'b1), .clk(CLOCK), .Q(register_3_q), .clr(R));
  Register register_4 (.D(in_2), .en(1'b1), .Q(register_4_q), .clr(R));  // open: clk
  // Probe on comparator_1_eq
  Comparator comparator_1 (.a(register_4_q), .b(in_1), .eq(comparator_1_eq));  // open: gt, lt
  // Probe on comparator_2_eq
  Comparator comparator_2 (.a(register_1_q), .b(in_1), .eq(comparator_2_eq));  // open: gt, lt
  // Probe on comparator_3_eq
  Comparator comparator_3 (.a(register_2_q), .b(in_1), .eq(comparator_3_eq));  // open: gt, lt
  // Probe on comparator_4_eq
  Comparator comparator_4 (.a(register_3_q), .b(in_1), .eq(comparator_4_eq));  // open: gt, lt
  // Probe on get_biggest_1_out_9
  get_biggest get_biggest_1 (.out_9(get_biggest_1_out_9));  // open: in_1, in_2, in_3, in_4, in_5, in_6, in_7, in_8
  Register register_5 (.D(in_3), .clk(button_2_out), .Q(register_5_q));  // open: en, clr
  Button button_2 (.out(button_2_out));
  Register register_6 (.D(in_3), .clk(button_3_out), .Q(register_6_q));  // open: en, clr
  Button button_3 (.out(button_3_out));
  Register register_7 (.D(in_3), .clk(button_4_out), .Q(register_7_q));  // open: en, clr
  Button button_4 (.out(button_4_out));
  Register register_8 (.D(in_3), .clk(button_5_out), .Q(register_8_q));  // open: en, clr
  Button button_5 (.out(button_5_out));
  assign controlled_buffer_1_out = comparator_1_eq ? register_8_q : 8'bz;  // Controlled_Buffer controlled_buffer_1
  assign controlled_buffer_1_out = comparator_2_eq ? register_5_q : 8'bz;  // Controlled_Buffer controlled_buffer_2
  assign controlled_buffer_1_out = comparator_3_eq ? register_6_q : 8'bz;  // Controlled_Buffer controlled_buffer_3
  assign controlled_buffer_1_out = comparator_4_eq ? register_7_q : 8'bz;  // Controlled_Buffer controlled_buffer_4
  // Probe on controlled_buffer_1_out
  // Probe on or_1_out
  or or_1 (or_1_out, comparator_1_eq, comparator_2_eq, comparator_3_eq, comparator_4_eq);

  // Notes on the sheet:
  //   Memory Address
  //   Data Output Bus
  //   Tag Compare
  //   Tag Allocator
  //   Data Store
  //   Data Write
  //   Data Output Bus
  //   Cache Hit
endmodule
