// Logisim project ALU.circ as structural Verilog: 1 circuit, main circuit ALU
module ALU (
  input  [31:0] A,
  input  [31:0] B,
  input  [5:0] ALUOp,
  input  [5:0] Func,
  input  [31:0] Imm,
  input  [4:0] Shamt,
  input  ALUSrc,
  output Zero,
  output [31:0] ALUResult
);

  wire comparator_1_lt, comparator_2_eq, comparator_2_gt, comparator_2_lt, comparator_3_gt, comparator_3_lt,
       or_3_out, or_4_out, or_5_out;
  wire [4:0] amount, bit_extender_1_out, bit_extender_2_out;
  wire [31:0] A_and_B, A_and_B_i, A_nor_B, A_nor_B_i, A_or_B, A_or_B_i, A_xor_B, A_xor_B_i, add, addi, addiu,
       addu, BEQ, BGEZ, BGTZ, BLEZ, BNE, div, mult, multiplexer_1_out, multiplexer_2_out, multiplexer_3_out,
       multiplexer_4_out, S_LL, S_LLV, S_RA, S_RL, S_RLV, SLT, SLTi, sub, subi, subu, undriven;

  assign A_xor_B = A ^ B;  // XOR_Gate xor_1, 32 bits wide
  assign A_or_B = A | B;  // OR_Gate or_1, 32 bits wide
  assign A_nor_B = ~(A | B);  // NOR_Gate nor_1, 32 bits wide
  assign A_and_B = A & B;  // AND_Gate and_1, 32 bits wide
  assign A_and_B_i = A & Imm;  // AND_Gate and_2, 32 bits wide
  assign A_or_B_i = A | Imm;  // OR_Gate or_2, 32 bits wide
  assign A_nor_B_i = ~(A | Imm);  // NOR_Gate nor_2, 32 bits wide
  assign A_xor_B_i = A ^ Imm;  // XOR_Gate xor_2, 32 bits wide
  Multiplexer #(.select(5), .width(32)) multiplexer_1 (
    .in0(add), .in1(addu), .in2(sub), .in3(subu), .in4(A_and_B), .in5(A_or_B), .in6(A_xor_B), .in7(A_nor_B),
    .in10(SLT), .out(multiplexer_1_out), .sel(Func[5:1]));  // open: in8, in9, in11, in12, in13, in14, in15, in16, in17, in18, in19, in20, in21, in22, in23, in24, in25, in26, in27, in28, in29, in30, in31
  Multiplexer #(.select(5), .width(32)) multiplexer_2 (
    .in0(S_LL), .in2(S_RL), .in3(S_RA), .in4(S_LLV), .in6(S_RLV), .in24(mult), .in26(div),
    .out(multiplexer_2_out), .sel(Func[5:1]));  // open: in1, in5, in7, in8, in9, in10, in11, in12, in13, in14, in15, in16, in17, in18, in19, in20, in21, in22, in23, in25, in27, in28, in29, in30, in31
  Multiplexer #(.width(32)) multiplexer_3 (
    .in0(multiplexer_2_out), .in1(multiplexer_1_out), .out(multiplexer_3_out), .sel(Func[0]));
  Multiplexer #(.select(5), .width(32)) multiplexer_4 (
    .in1(BGEZ), .in4(BEQ), .in5(BNE), .in6(BLEZ), .in7(BGTZ), .in8(addi), .in9(addiu), .in10(SLTi),
    .in12(A_and_B_i), .in13(A_or_B_i), .in14(A_xor_B_i), .in15({Imm[15:0], {16{1'b0}}}), .in16(undriven),
    .out(multiplexer_4_out), .sel(ALUOp[5:1]));  // open: in0, in2, in3, in11, in17, in18, in19, in20, in21, in22, in23, in24, in25, in26, in27, in28, in29, in30, in31
  Adder #(.width(32)) adder_1 (.a(A), .b(B), .out(add));  // open: cin, cout
  Subtractor #(.width(32)) subtractor_1 (.a(A), .b(B), .out(sub));  // open: bin, bout
  Adder #(.width(32)) adder_2 (.a(A), .b(Imm), .out(addi));  // open: cin, cout
  Subtractor #(.width(32)) subtractor_2 (.a(A), .b(Imm), .out(subi));  // open: bin, bout
  Adder #(.width(32)) adder_3 (.a(A), .b(B), .out(addu));  // open: cin, cout
  Subtractor #(.width(32)) subtractor_3 (.a(A), .b(B), .out(subu));  // open: bin, bout
  Adder #(.width(32)) adder_4 (.a(A), .b(Imm), .out(addiu));  // open: cin, cout
  Multiplier #(.width(32)) multiplier_1 (.a(A), .b(B), .out(mult));  // open: cin, cout
  Divider #(.width(32)) divider_1 (.a(A), .b(B), .out(div));  // open: upper, rem
  Multiplexer #(.width(32)) multiplexer_5 (
    .in0(multiplexer_3_out), .in1(multiplexer_4_out), .out(ALUResult), .sel(ALUSrc));
  Bit_Extender #(.in_width(32), .out_width(5)) bit_extender_1 (.in(B), .out(bit_extender_1_out));
  Bit_Extender #(.in_width(32), .out_width(5)) bit_extender_2 (.in(B), .out(bit_extender_2_out));
  Comparator #(.width(32)) comparator_1 (.a(A), .b(Imm), .lt(comparator_1_lt));  // open: gt, eq
  Shifter #(.width(32)) shifter_1 (.in(A), .\dist (amount), .out(S_LL));
  Shifter #(.width(32)) shifter_2 (.in(A), .\dist (bit_extender_1_out), .out(S_LLV));
  Shifter #(.shift("lr"), .width(32)) shifter_3 (.in(A), .\dist (amount), .out(S_RL));
  Shifter #(.shift("ar"), .width(32)) shifter_4 (.in(A), .\dist (amount), .out(S_RA));
  Shifter #(.shift("lr"), .width(32)) shifter_5 (.in(A), .\dist (bit_extender_2_out), .out(S_RLV));
  assign SLTi = {{31{comparator_1_lt}}, comparator_1_lt};  // Bit_Extender bit_extender_3
  Comparator #(.width(32)) comparator_2 (
    .a(A), .b({32{1'b0}}), .gt(comparator_2_gt), .eq(comparator_2_eq), .lt(comparator_2_lt));
  Comparator #(.width(32)) comparator_3 (.a(A), .b(B), .gt(comparator_3_gt), .eq(Zero), .lt(comparator_3_lt));
  assign BGTZ = {{31{comparator_2_gt}}, comparator_2_gt};  // Bit_Extender bit_extender_4
  or or_3 (or_3_out, comparator_2_gt, comparator_2_eq);
  or or_4 (or_4_out, comparator_2_eq, comparator_2_lt);
  or or_5 (or_5_out, comparator_3_gt, comparator_3_lt);
  assign BEQ = {{31{Zero}}, Zero};  // Bit_Extender bit_extender_5
  assign SLT = {{31{comparator_3_lt}}, comparator_3_lt};  // Bit_Extender bit_extender_6
  assign BGEZ = {{31{or_3_out}}, or_3_out};  // Bit_Extender bit_extender_7
  assign BLEZ = {{31{or_4_out}}, or_4_out};  // Bit_Extender bit_extender_8
  assign BNE = {{31{or_5_out}}, or_5_out};  // Bit_Extender bit_extender_9

  // Other names for the same wires on the sheet: Iui[31:16] = Imm[15:0]

  // Notes on the sheet:
  //   SLL
  //   SLLV
  //   SRL
  //   SRA
  //   SRLV
endmodule
