// Logisim project ControlUnit.circ as structural Verilog: 1 circuit, main circuit CU
module CU (
  input  [5:0] Func,
  input  [5:0] Opcode,
  output ALUSrc,
  output [5:0] ALUop,
  output RegDst,
  output ALU_V,
  output MemToReg,
  output RegWrite,
  output [3:0] MemWriteMask,
  output Branch,
  output Jump
);

  wire and_2_out, and_3_out, and_4_out, and_5_out, and_6_out, and_7_out, and_8_out, and_9_out, and_10_out,
       and_11_out, and_12_out, and_13_out, and_14_out, and_15_out, and_16_out, and_17_out, and_18_out,
       and_19_out, and_21_out, and_22_out, and_23_out, not_1_out, not_2_out, not_3_out, not_4_out, not_5_out,
       not_6_out, not_7_out, not_8_out, not_9_out, not_10_out, not_11_out, not_12_out, not_13_out, or_3_out;

  not not_1 (not_1_out, Opcode[0]);
  not not_2 (not_2_out, Opcode[1]);
  not not_3 (not_3_out, Opcode[2]);
  not not_4 (not_4_out, Opcode[3]);
  not not_5 (not_5_out, Opcode[4]);
  not not_6 (not_6_out, Opcode[5]);
  and and_1 (RegDst, not_1_out, not_2_out, not_3_out, not_4_out, not_5_out, not_6_out);
  // OR_Gate or_1: pin names not known; wires that end beside it: Opcode[0], Opcode[1], Opcode[2], Opcode[3], Opcode[4], Opcode[5], ALUSrc
  and and_2 (and_2_out, Opcode[0], Opcode[1], not_3_out, not_4_out, not_5_out, Opcode[5]);
  and and_3 (and_3_out, Opcode[0], Opcode[1], not_3_out, Opcode[3], not_5_out, Opcode[5]);
  and and_4 (and_4_out, not_1_out, not_2_out, not_3_out, not_4_out, not_5_out, Opcode[5]);
  and and_5 (and_5_out, not_1_out, not_2_out, not_3_out, Opcode[3], not_5_out, Opcode[5]);
  and and_6 (and_6_out, Opcode[0], Opcode[1], Opcode[2], Opcode[3], not_5_out, not_6_out);
  and and_7 (and_7_out, not_1_out, not_2_out, Opcode[2], not_4_out, not_5_out, not_6_out);
  and and_8 (and_8_out, Opcode[0], not_2_out, Opcode[2], not_4_out, not_5_out, not_6_out);
  and and_9 (and_9_out, not_1_out, Opcode[1], Opcode[2], not_4_out, not_5_out, not_6_out);
  and and_10 (and_10_out, Opcode[0], Opcode[1], Opcode[2], not_4_out, not_5_out, not_6_out);
  and and_11 (and_11_out, Opcode[0], not_2_out, not_3_out, not_4_out, not_5_out, not_6_out);
  and and_12 (and_12_out, not_1_out, not_2_out, not_3_out, Opcode[3], not_5_out, not_6_out);
  and and_13 (and_13_out, Opcode[0], not_2_out, not_3_out, Opcode[3], not_5_out, not_6_out);
  and and_14 (and_14_out, not_1_out, not_2_out, Opcode[2], Opcode[3], not_5_out, not_6_out);
  and and_15 (and_15_out, not_1_out, Opcode[1], Opcode[2], Opcode[3], not_5_out, not_6_out);
  and and_16 (and_16_out, Opcode[0], not_2_out, Opcode[2], Opcode[3], not_5_out, not_6_out);
  and and_17 (and_17_out, not_1_out, Opcode[1], not_3_out, Opcode[3], not_5_out, not_6_out);
  and and_18 (and_18_out, not_1_out, Opcode[1], not_3_out, not_4_out, not_5_out, not_6_out);
  and and_19 (and_19_out, Opcode[0], Opcode[1], not_3_out, not_4_out, not_5_out, not_6_out);
  or or_2 (MemToReg, and_2_out, and_4_out);
  or or_3 (or_3_out, and_2_out, and_4_out, and_6_out, RegDst, and_12_out, and_13_out, and_14_out, and_15_out, and_16_out, and_17_out, and_19_out);
  and and_20 (MemWriteMask[3], and_2_out, and_3_out);
  and and_21 (and_21_out, and_4_out, and_5_out);
  or or_4 (Branch, and_7_out, and_8_out, and_9_out, and_10_out, and_11_out);
  or or_5 (Jump, and_18_out, and_19_out);
  or or_6 (MemWriteMask[0], MemWriteMask[3], and_21_out);
  not not_7 (not_7_out, Func[0]);
  not not_8 (not_8_out, Func[1]);
  not not_9 (not_9_out, Func[2]);
  not not_10 (not_10_out, Func[3]);
  not not_11 (not_11_out, Func[4]);
  not not_12 (not_12_out, Func[5]);
  and and_22 (and_22_out, not_7_out, not_8_out, not_9_out, Func[3], not_11_out, not_12_out);
  not not_13 (not_13_out, and_22_out);
  and and_23 (and_23_out, Func[0], Func[1], not_9_out, not_10_out, not_11_out, not_12_out);
  and and_24 (RegWrite, not_13_out, or_3_out);
  nor nor_1 (ALU_V, and_19_out, and_23_out);

  assign ALUop = Opcode;
  assign MemWriteMask[2:1] = {2{MemWriteMask[3]}};

  // Notes on the sheet:
  //   R_format
  //   lw
  //   sw
  //   lB
  //   SB
  //   lui
  //   beq
  //   bne
  //   blez
  //   bgtz
  //   bgez
  //   addi
  //   addiu
  //   andi
  //   xori
  //   ori
  //   slti
  //   J
  //   JAL
  //   Jr
  //   Syscall
endmodule
