// Logisim project JrControl.circ as structural Verilog: 1 circuit, main circuit JCU
module JCU (
  input  [5:0] Func,
  input  [31:0] in1,
  input  [4:0] rs,
  output [31:0] Y
);

  wire JR, not_1_out, not_2_out, not_3_out, not_4_out, not_5_out;

  not not_1 (not_1_out, Func[0]);
  not not_2 (not_2_out, Func[1]);
  not not_3 (not_3_out, Func[2]);
  not not_4 (not_4_out, Func[4]);
  not not_5 (not_5_out, Func[5]);
  and and_1 (JR, not_1_out, not_2_out, not_3_out, Func[3], not_4_out, not_5_out);
  Multiplexer #(.width(32)) multiplexer_1 (.in0(in1), .in1({{27{1'b0}}, rs}), .out(Y), .sel(JR));

  // Notes on the sheet:
  //   Jr
endmodule
