// Logisim project MUX2x1.circ as structural Verilog: 1 circuit, main circuit MUX2x1
module MUX2x1 (
  input  X0,
  input  X1,
  input  Sel,
  output Y
);

  wire and_1_out, and_2_out, dec11_1_h0, dec11_1_h1;

  dec11 dec11_1 (.S(Sel), .H0(dec11_1_h0), .H1(dec11_1_h1));
  and and_1 (and_1_out, X0, dec11_1_h0);
  and and_2 (and_2_out, X1, dec11_1_h1);
  or or_1 (Y, and_1_out, and_2_out);
endmodule
