// Logisim project ProgramCounter.circ as structural Verilog: 1 circuit, main circuit ProgramCounter
module ProgramCounter (
  input  En,
  input  CLK,
  input  [31:0] PC_in,
  output [31:0] PC_out
);

  Hex_Digit_Display #(.decimalPoint("false")) hex_digit_display_1 (.value(PC_in[31:28]));
  Hex_Digit_Display #(.decimalPoint("false")) hex_digit_display_2 (.value(PC_in[27:24]));
  Hex_Digit_Display #(.decimalPoint("false")) hex_digit_display_3 (.value(PC_in[23:20]));
  Register #(.width(32)) PC (.D(PC_in), .en(En), .clk(CLK), .Q(PC_out));  // open: clr
  Hex_Digit_Display #(.decimalPoint("false")) hex_digit_display_4 (.value(PC_in[19:16]));
  Hex_Digit_Display #(.decimalPoint("false")) hex_digit_display_5 (.value(PC_in[15:12]));
  Hex_Digit_Display #(.decimalPoint("false")) hex_digit_display_6 (.value(PC_in[11:8]));
  Hex_Digit_Display #(.decimalPoint("false")) hex_digit_display_7 (.value(PC_in[7:4]));
  Hex_Digit_Display #(.decimalPoint("false")) hex_digit_display_8 (.value(PC_in[3:0]));
  Hex_Digit_Display #(.decimalPoint("false")) hex_digit_display_9 (.value(PC_out[31:28]));
  Hex_Digit_Display #(.decimalPoint("false")) hex_digit_display_10 (.value(PC_out[27:24]));
  Hex_Digit_Display #(.decimalPoint("false")) hex_digit_display_11 (.value(PC_out[23:20]));
  Hex_Digit_Display #(.decimalPoint("false")) hex_digit_display_12 (.value(PC_out[19:16]));
  Hex_Digit_Display #(.decimalPoint("false")) hex_digit_display_13 (.value(PC_out[15:12]));
  Hex_Digit_Display #(.decimalPoint("false")) hex_digit_display_14 (.value(PC_out[11:8]));
  Hex_Digit_Display #(.decimalPoint("false")) hex_digit_display_15 (.value(PC_out[7:4]));
  Hex_Digit_Display #(.decimalPoint("false")) hex_digit_display_16 (.value(PC_out[3:0]));
endmodule
