// Logisim project SE.circ as structural Verilog: 1 circuit, main circuit SignExtend
module SignExtend (
  input  [15:0] S16,
  output [31:0] S32
);


  assign S32 = {{17{S16[15]}}, S16[14:0]};
endmodule
