// Logisim project SHL.circ as structural Verilog: 1 circuit, main circuit shiftLeffBy2
module shiftLeffBy2 (
  input  [31:0] in_1,
  output [31:0] Y
);

  Shifter #(.width(32)) shifter_1 (.in(in_1), .\dist (5'b00010), .out(Y));
endmodule
