// Logisim project adder_32bit.circ as structural Verilog: 1 circuit, main circuit Adder_32bit
module Adder_32bit (
  input  [31:0] A,
  input  [31:0] B,
  output [31:0] Result
);

  wire adder_1_cout;

  // Probe on adder_1_cout
  Adder #(.width(32)) adder_1 (.a(A), .b(B), .out(Result), .cin(1'b0), .cout(adder_1_cout));
endmodule
