// Logisim project aluuu.circ as structural Verilog: 1 circuit, main circuit main
module main (
  input  [5:0] func,
  input  [5:0] opcode,
  input  [31:0] A,
  input  [31:0] B,
  input  [31:0] pc,
  input  R_or_i,
  input  [4:0] amount,
  input  [15:0] imm,
  input  [31:0] not_input,
  output [31:0] javab,
  output [31:0] out_11
);

  wire A_bish_B, A_bish_zero, A_equ_B, A_equ_zero, A_kam_B, A_kam_zero, comparator_3_gt, not_1_out,
       not_2_out, not_3_out;
  wire [4:0] amount_t, bit_extender_8_out, bit_extender_9_out;
  wire [31:0] A_and_B, A_and_B_i, A_nor_B, A_nor_B_i, A_or_B, A_or_B_i, A_xor_B, A_xor_B_i, add, adder_1_out,
       adder_2_out, adder_3_out, adder_4_out, adder_5_out, addi, addu, BEQ_T, BGTZ_T, bit_extender_2_out,
       bit_extender_3_out, bit_extender_4_out, bit_extender_5_out, bit_extender_6_out, bit_extender_7_out,
       bit_extender_10_out, bit_extender_11_out, bit_extender_12_out, bit_extender_13_out, BLEZ_T, BNE_T,
       div, mult, multiplexer_6_out, multiplexer_8_out, multiplexer_9_out, multiplexer_10_out,
       multiplexer_11_out, R_2, R_3, R_4, R_6, R_7, R_18, sub, subu, syscall, undriven, undriven_2,
       undriven_3, undriven_4, undriven_5, undriven_6, undriven_7;

  Bit_Extender #(.in_width(16), .out_width(32)) bit_extender_1 ();  // open: in, out
  Comparator #(.width(32)) comparator_1 (.a(A), .b(B), .gt(A_bish_B), .eq(A_equ_B), .lt(A_kam_B));
  Comparator #(.width(32)) comparator_2 (.a(A), .b(not_input), .gt(A_bish_zero), .eq(A_equ_zero), .lt(A_kam_zero));
  assign bit_extender_2_out = {{16{imm[15]}}, imm};  // Bit_Extender bit_extender_2
  assign bit_extender_3_out = {{16{imm[15]}}, imm};  // Bit_Extender bit_extender_3
  assign bit_extender_4_out = {{16{imm[15]}}, imm};  // Bit_Extender bit_extender_4
  assign bit_extender_5_out = {{16{imm[15]}}, imm};  // Bit_Extender bit_extender_5
  assign bit_extender_6_out = {{16{imm[15]}}, imm};  // Bit_Extender bit_extender_6
  assign bit_extender_7_out = {{16{imm[15]}}, imm};  // Bit_Extender bit_extender_7
  Bit_Extender #(.in_width(32), .out_width(5)) bit_extender_8 (.in(B), .out(bit_extender_8_out));
  Bit_Extender #(.in_width(32), .out_width(5)) bit_extender_9 (.in(B), .out(bit_extender_9_out));
  Comparator #(.width(32)) comparator_3 (.a(A), .b(B), .gt(comparator_3_gt));  // open: eq, lt
  assign bit_extender_10_out = {{16{imm[15]}}, imm};  // Bit_Extender bit_extender_10
  Adder #(.width(32)) adder_1 (.a(pc), .b(bit_extender_11_out), .out(adder_1_out));  // open: cin, cout
  assign bit_extender_11_out = {{16{imm[15]}}, imm};  // Bit_Extender bit_extender_11
  Adder #(.width(32)) adder_2 (.a(pc), .b(bit_extender_12_out), .out(adder_2_out));  // open: cin, cout
  assign bit_extender_12_out = {{16{imm[15]}}, imm};  // Bit_Extender bit_extender_12
  Adder #(.width(32)) adder_3 (.a(pc), .b(bit_extender_13_out), .out(adder_3_out));  // open: cin, cout
  assign bit_extender_13_out = {{16{imm[15]}}, imm};  // Bit_Extender bit_extender_13
  Adder #(.width(32)) adder_4 (.a(pc), .b(bit_extender_6_out), .out(adder_4_out));  // open: cin, cout
  not not_1 (not_1_out, A_kam_zero);
  Adder #(.width(32)) adder_5 (.a(pc), .b(bit_extender_7_out), .out(adder_5_out));  // open: cin, cout
  assign A_xor_B = A ^ B;  // XOR_Gate xor_1, 32 bits wide
  Shifter #(.width(32)) shifter_1 (.in(A), .\dist (amount_t), .out(R_2));
  Shifter #(.width(32)) shifter_2 (.in(A), .\dist (bit_extender_8_out), .out(R_3));
  Shifter #(.shift("lr"), .width(32)) shifter_3 (.in(A), .\dist (amount_t), .out(R_4));
  Subtractor #(.width(32)) subtractor_1 (.a(A), .b(B), .out(sub));  // open: bin, bout
  Shifter #(.shift("lr"), .width(32)) shifter_4 (.in(A), .\dist (bit_extender_9_out), .out(R_6));
  assign R_7 = {{31{comparator_3_gt}}, comparator_3_gt};  // Bit_Extender bit_extender_14
  Subtractor #(.width(32)) subtractor_2 (.a(A), .b(B), .out(subu));  // open: bin, bout
  assign A_or_B = A | B;  // OR_Gate or_1, 32 bits wide
  assign A_nor_B = ~(A | B);  // NOR_Gate nor_1, 32 bits wide
  Adder #(.width(32)) adder_6 (.a(A), .b(B), .out(add));  // open: cin, cout
  Multiplier #(.width(32)) multiplier_1 (.a(A), .b(B), .out(mult));  // open: cin, cout
  Divider #(.width(32)) divider_1 (.a(A), .b(B), .out(div));  // open: upper, rem
  assign A_and_B = A & B;  // AND_Gate and_1, 32 bits wide
  Adder #(.width(32)) adder_7 (.a(A), .b(B), .out(addu));  // open: cin, cout
  Shifter #(.shift("lr"), .width(32)) shifter_5 (.in(A), .\dist (amount_t), .out(R_18));
  Adder #(.width(32)) adder_8 (.a(A), .b(bit_extender_10_out), .out(addi));  // open: cin, cout
  assign A_and_B_i = A & bit_extender_2_out;  // AND_Gate and_2, 32 bits wide
  assign A_or_B_i = A | bit_extender_3_out;  // OR_Gate or_2, 32 bits wide
  assign A_nor_B_i = ~(A | bit_extender_4_out);  // NOR_Gate nor_2, 32 bits wide
  assign A_xor_B_i = A ^ bit_extender_5_out;  // XOR_Gate xor_2, 32 bits wide
  Multiplexer #(.width(32)) multiplexer_1 (.in0(pc), .in1(adder_1_out), .out(BEQ_T), .sel(A_equ_B));
  Multiplexer #(.width(32)) multiplexer_2 (.in0(pc), .in1(adder_2_out), .out(BNE_T), .sel(not_2_out));
  not not_2 (not_2_out, A_equ_B);
  Multiplexer #(.width(32)) multiplexer_3 (.in0(pc), .in1(adder_3_out), .out(BLEZ_T), .sel(not_3_out));
  not not_3 (not_3_out, A_bish_zero);
  Multiplexer #(.width(32)) multiplexer_4 (.in0(pc), .in1(adder_4_out), .out(BGTZ_T), .sel(A_bish_zero));
  Multiplexer #(.width(32)) multiplexer_5 (.in0(pc), .in1(adder_5_out), .out(BLEZ_T), .sel(not_1_out));
  Multiplexer #(.select(5), .width(32)) multiplexer_6 (
    .in1(R_2), .in2(R_4), .in3(R_18), .in4(R_3), .in6(R_6), .in8(undriven_6), .in12(syscall), .in24(mult),
    .in26(div), .out(multiplexer_6_out), .sel(func[4:0]));  // open: in0, in5, in7, in9, in10, in11, in13, in14, in15, in16, in17, in18, in19, in20, in21, in22, in23, in25, in27, in28, in29, in30, in31
  Multiplexer #(.select(5), .width(32)) multiplexer_7 (
    .in0(add), .in1(addu), .in2(sub), .in3(subu), .in4(A_and_B), .in5(A_or_B), .in7(A_nor_B), .in10(R_7),
    .sel(func[4:0]));  // open: in6, in8, in9, in11, in12, in13, in14, in15, in16, in17, in18, in19, in20, in21, in22, in23, in24, in25, in26, in27, in28, in29, in30, in31, out
  Multiplexer #(.select(5), .width(32)) multiplexer_8 (
    .in1(BLEZ_T), .in4(BEQ_T), .in5(BNE_T), .in6(BLEZ_T), .in7(BGTZ_T), .in8(addi), .in9(addi),
    .in10(undriven), .in12(A_and_B_i), .in13(A_or_B_i), .in14(A_xor_B_i), .out(multiplexer_8_out),
    .sel(opcode[4:0]));  // open: in0, in2, in3, in11, in15, in16, in17, in18, in19, in20, in21, in22, in23, in24, in25, in26, in27, in28, in29, in30, in31
  Multiplexer #(.select(5), .width(32)) multiplexer_9 (
    .in0(undriven_2), .in3(undriven_3), .in8(undriven_4), .in11(undriven_5), .out(multiplexer_9_out),
    .sel(opcode[4:0]));  // open: in1, in2, in4, in5, in6, in7, in9, in10, in12, in13, in14, in15, in16, in17, in18, in19, in20, in21, in22, in23, in24, in25, in26, in27, in28, in29, in30, in31
  Multiplexer #(.width(32)) multiplexer_10 (
    .in0(multiplexer_6_out), .in1(undriven_7), .out(multiplexer_10_out), .sel(func[5]));
  Multiplexer #(.width(32)) multiplexer_11 (
    .in0(multiplexer_8_out), .in1(multiplexer_9_out), .out(multiplexer_11_out), .sel(opcode[5]));
  Multiplexer #(.width(32)) multiplexer_12 (
    .in0(multiplexer_10_out), .in1(multiplexer_11_out), .out(javab), .sel(R_or_i));

  // Other names for the same wires on the sheet: amoubt[4:0] = amount; func5[4:0] = func[4:0];
  //   opcode5[4:0] = opcode[4:0]; zero[31:0] = not_input
endmodule
