// Logisim project block.circ as structural Verilog: 1 circuit, main circuit B_lock
module B_lock (
  input  [31:0] data_in,
  input  [1:0] word_index,
  input  CLOCK,
  input  RESET,
  output hit
);

  wire and_1_out, and_2_out, and_3_out, and_4_out, comparator_1_eq, comparator_2_eq, comparator_3_eq,
       comparator_4_eq, decoder_1_out0, decoder_1_out1, decoder_1_out2, decoder_1_out3, or_2_out, V;
  wire [7:0] register_1_q, register_5_q, register_9_q, register_13_q;

  Decoder #(.select(2)) decoder_1 (
    .out0(decoder_1_out0), .out1(decoder_1_out1), .out2(decoder_1_out2), .out3(decoder_1_out3),
    .sel(word_index), .en(1'b1));
  and and_1 (and_1_out, CLOCK, decoder_1_out0);
  and and_2 (and_2_out, CLOCK, decoder_1_out1);
  and and_3 (and_3_out, CLOCK, decoder_1_out2);
  and and_4 (and_4_out, CLOCK, decoder_1_out3);
  or or_1 (V, and_1_out, and_2_out, and_3_out, and_4_out);
  Register register_1 (.D(data_in[7:0]), .en(1'b1), .clk(and_1_out), .Q(register_1_q), .clr(RESET));
  Register register_2 (.D(data_in[7:0]), .en(1'b1), .clk(and_2_out), .Q(register_1_q), .clr(RESET));
  Register register_3 (.D(data_in[7:0]), .en(1'b1), .clk(and_3_out), .Q(register_1_q), .clr(RESET));
  Register register_4 (.D(data_in[7:0]), .en(1'b1), .clk(and_4_out), .Q(register_1_q), .clr(RESET));
  Comparator #(.mode("unsigned")) comparator_1 (
    .a(register_1_q), .b(data_in[7:0]), .eq(comparator_1_eq));  // open: gt, lt
  Register register_5 (.D(data_in[15:8]), .en(1'b1), .clk(and_1_out), .Q(register_5_q), .clr(RESET));
  Register register_6 (.D(data_in[15:8]), .en(1'b1), .clk(and_2_out), .clr(RESET));  // open: Q
  Register register_7 (.D(data_in[15:8]), .en(1'b1), .clk(and_3_out), .clr(RESET));  // open: Q
  Register register_8 (.D(data_in[15:8]), .en(1'b1), .clk(and_4_out), .clr(RESET));  // open: Q
  Comparator #(.mode("unsigned")) comparator_2 (
    .a(register_5_q), .b(data_in[15:8]), .eq(comparator_2_eq));  // open: gt, lt
  Register register_9 (.D(data_in[23:16]), .en(1'b1), .clk(and_1_out), .Q(register_9_q), .clr(RESET));
  Register register_10 (.D(data_in[23:16]), .en(1'b1), .clk(and_2_out), .Q(register_9_q), .clr(RESET));
  Register register_11 (.D(data_in[23:16]), .en(1'b1), .clk(and_3_out), .Q(register_9_q), .clr(RESET));
  Register register_12 (.D(data_in[23:16]), .en(1'b1), .clk(and_4_out), .Q(register_9_q), .clr(RESET));
  Comparator #(.mode("unsigned")) comparator_3 (
    .a(register_9_q), .b(data_in[23:16]), .eq(comparator_3_eq));  // open: gt, lt
  Register register_13 (.D(data_in[31:24]), .en(1'b1), .clk(and_1_out), .Q(register_13_q), .clr(RESET));
  Register register_14 (.D(data_in[31:24]), .en(1'b1), .clk(and_2_out), .Q(register_13_q), .clr(RESET));
  Register register_15 (.D(data_in[31:24]), .en(1'b1), .clk(and_3_out), .Q(register_13_q), .clr(RESET));
  Register register_16 (.D(data_in[31:24]), .en(1'b1), .clk(and_4_out), .Q(register_13_q), .clr(RESET));
  Comparator #(.mode("unsigned")) comparator_4 (
    .a(register_13_q), .b(data_in[31:24]), .eq(comparator_4_eq));  // open: gt, lt
  or or_2 (or_2_out, comparator_4_eq, comparator_3_eq, comparator_2_eq, comparator_1_eq);
  and and_5 (hit, or_2_out, V);

  // Notes on the sheet:
  //   w1
  //   w2
  //   w3
  //   w4
endmodule
