// Logisim project cache.circ as structural Verilog: 1 circuit, main circuit cache
module cache (
  input  [31:0] CPU_Address,
  input  [31:0] memWriteData,
  input  [3:0] MemWriteMask,
  input  LRU,
  input  clock,
  input  reset,
  output [31:0] raedData,
  output Hit,
  output LRU_out,
  output [3:0] writeMask
);

  wire and_5_out, and_6_out, and_7_out, and_8_out, and_9_out, and_10_out, and_11_out, and_12_out, and_13_out,
       and_14_out, and_15_out, and_16_out, and_17_out, and_18_out, and_19_out, and_20_out, and_21_out,
       and_22_out, and_23_out, and_24_out, and_25_out, and_26_out, and_27_out, and_28_out, and_29_out,
       and_30_out, and_31_out, and_32_out, and_33_out, and_34_out, and_35_out, and_36_out, and_37_out,
       and_38_out, and_39_out, and_40_out, and_41_out, and_42_out, and_43_out, block_index, clock1, clock2,
       clock3, clock4, comparator_1_eq, comparator_2_eq, comparator_3_eq, comparator_4_eq, comparator_5_eq,
       comparator_6_eq, comparator_7_eq, comparator_8_eq, dirty_b11, dirty_b12, dirty_b21, dirty_b22,
       dirty_b31, dirty_b32, dirty_b41, dirty_b42, hit1, hit2, hit3, hit4, not_1_out, not_2_out, not_3_out,
       not_4_out, not_5_out, not_6_out, not_7_out, not_8_out, not_9_out, not_10_out, not_11_out, not_12_out,
       not_13_out, not_14_out, not_15_out, not_16_out, not_17_out, not_18_out, not_19_out, not_20_out,
       not_21_out, not_22_out, not_23_out, not_24_out, not_25_out, not_26_out, not_27_out, or_4_out,
       or_5_out, or_6_out, or_7_out, or_8_out, or_9_out, or_10_out, or_11_out, or_16_out, or_17_out,
       or_18_out, or_19_out, or_20_out, set1, set2, set3, set4, v11, v12, v21, v22, v31, v32, v41, v42, write;
  wire [27:0] register_17_q, register_18_q, register_19_q, register_20_q, register_21_q, register_22_q,
       register_23_q, register_24_q;

  Decoder #(.select(2)) decoder_1 (
    .out0(set1), .out1(set2), .out2(set3), .out3(set4), .sel(CPU_Address[3:2]), .en(1'b1));
  or or_1 (write, MemWriteMask[0], MemWriteMask[1], MemWriteMask[2], MemWriteMask[3]);
  and and_1 (clock1, clock, set1);
  and and_2 (clock2, clock, set2);
  and and_3 (clock3, clock, set3);
  and and_4 (clock4, clock, set4);
  set set_1 (
    .data_in(memWriteData), .word_index(CPU_Address[1:0]), .block_index(block_index),
    .MemWriteMask(MemWriteMask), .CLOCK(clock1), .RESET(reset), .MemReadData(raedData));
  set set_2 (
    .data_in(memWriteData), .word_index(CPU_Address[1:0]), .block_index(block_index),
    .MemWriteMask(MemWriteMask), .CLOCK(clock2), .RESET(reset), .MemReadData(raedData));
  set set_3 (
    .data_in(memWriteData), .word_index(CPU_Address[1:0]), .block_index(block_index),
    .MemWriteMask(MemWriteMask), .CLOCK(clock3), .RESET(reset), .MemReadData(raedData));
  set set_4 (
    .data_in(memWriteData), .word_index(CPU_Address[1:0]), .block_index(block_index),
    .MemWriteMask(MemWriteMask), .CLOCK(clock4), .RESET(reset), .MemReadData(raedData));
  or or_2 (Hit, hit1, hit2, hit3, hit4);
  not not_1 (not_1_out, Hit);
  not not_2 (not_2_out, block_index);
  not not_3 (not_3_out, block_index);
  not not_4 (not_4_out, block_index);
  not not_5 (not_5_out, block_index);
  not not_6 (not_6_out, LRU);
  and and_5 (and_5_out, not_1_out, not_6_out);
  Register #(.width(1)) register_1 (.D(1'b1), .en(and_6_out), .clk(clock1), .Q(v11), .clr(reset));
  and and_6 (and_6_out, write, not_2_out, set1);
  Register #(.width(1)) register_2 (.D(1'b1), .en(and_7_out), .clk(clock1), .Q(v12), .clr(reset));
  and and_7 (and_7_out, write, block_index, set1);
  Register #(.width(1)) register_3 (.D(1'b1), .en(and_8_out), .clk(clock2), .Q(v21), .clr(reset));
  and and_8 (and_8_out, write, not_3_out, set2);
  Register #(.width(1)) register_4 (.D(1'b1), .en(and_9_out), .clk(clock2), .Q(v22), .clr(reset));
  and and_9 (and_9_out, write, block_index, set2);
  Register #(.width(1)) register_5 (.D(1'b1), .en(and_10_out), .clk(clock3), .Q(v31), .clr(reset));
  and and_10 (and_10_out, write, not_4_out, set3);
  Register #(.width(1)) register_6 (.D(1'b1), .en(and_11_out), .clk(clock3), .Q(v32), .clr(reset));
  and and_11 (and_11_out, write, block_index, set3);
  Register #(.width(1)) register_7 (.D(1'b1), .en(and_12_out), .clk(clock4), .Q(v41), .clr(reset));
  and and_12 (and_12_out, write, not_5_out, set4);
  Register #(.width(1)) register_8 (.D(1'b1), .en(and_13_out), .clk(clock4), .Q(v42), .clr(reset));
  and and_13 (and_13_out, write, block_index, set4);
  and and_14 (and_14_out, LRU, Hit);
  or or_3 (LRU_out, and_14_out, and_5_out);
  not not_7 (not_7_out, block_index);
  not not_8 (not_8_out, block_index);
  not not_9 (not_9_out, block_index);
  not not_10 (not_10_out, block_index);
  not not_11 (not_11_out, hit1);
  not not_12 (not_12_out, hit2);
  not not_13 (not_13_out, hit3);
  not not_14 (not_14_out, hit4);
  Register #(.width(1)) register_9 (.D(1'b1), .en(and_15_out), .clk(clock1), .Q(dirty_b11), .clr(or_4_out));
  and and_15 (and_15_out, hit1, write, not_7_out);
  Register #(.width(1)) register_10 (.D(1'b1), .en(and_16_out), .clk(clock1), .Q(dirty_b12), .clr(or_5_out));
  and and_16 (and_16_out, hit1, write, block_index);
  and and_17 (and_17_out, not_11_out, block_index);
  Register #(.width(1)) register_11 (.D(1'b1), .en(and_18_out), .clk(clock2), .Q(dirty_b21), .clr(or_6_out));
  and and_18 (and_18_out, hit2, write, not_8_out);
  Register #(.width(1)) register_12 (.D(1'b1), .en(and_19_out), .clk(clock2), .Q(dirty_b22), .clr(or_7_out));
  and and_19 (and_19_out, hit2, write, block_index);
  and and_20 (and_20_out, not_12_out, block_index);
  Register #(.width(1)) register_13 (.D(1'b1), .en(and_21_out), .clk(clock3), .Q(dirty_b31), .clr(or_8_out));
  and and_21 (and_21_out, hit3, write, not_9_out);
  Register #(.width(1)) register_14 (.D(1'b1), .en(and_22_out), .clk(clock3), .Q(dirty_b32), .clr(or_9_out));
  and and_22 (and_22_out, hit3, write, block_index);
  and and_23 (and_23_out, not_13_out, block_index);
  Register #(.width(1)) register_15 (.D(1'b1), .en(and_24_out), .clk(clock4), .Q(dirty_b41), .clr(or_10_out));
  and and_24 (and_24_out, hit4, write, not_10_out);
  Register #(.width(1)) register_16 (.D(1'b1), .en(and_25_out), .clk(clock4), .Q(dirty_b42), .clr(or_11_out));
  and and_25 (and_25_out, hit4, write, block_index);
  and and_26 (and_26_out, not_14_out, block_index);
  or or_4 (or_4_out, not_15_out, reset);
  or or_5 (or_5_out, and_17_out, reset);
  not not_15 (not_15_out, and_17_out);
  or or_6 (or_6_out, not_16_out, reset);
  or or_7 (or_7_out, and_20_out, reset);
  not not_16 (not_16_out, and_20_out);
  or or_8 (or_8_out, not_17_out, reset);
  or or_9 (or_9_out, and_23_out, reset);
  not not_17 (not_17_out, and_23_out);
  or or_10 (or_10_out, not_18_out, reset);
  or or_11 (or_11_out, and_26_out, reset);
  not not_18 (not_18_out, and_26_out);
  not not_19 (not_19_out, LRU);
  not not_20 (not_20_out, LRU);
  not not_21 (not_21_out, LRU);
  not not_22 (not_22_out, LRU);
  and and_27 (and_27_out, not_23_out, not_19_out);
  and and_28 (and_28_out, not_23_out, LRU);
  and and_29 (and_29_out, not_24_out, not_20_out);
  and and_30 (and_30_out, not_24_out, LRU);
  and and_31 (and_31_out, not_25_out, not_21_out);
  and and_32 (and_32_out, not_25_out, LRU);
  and and_33 (and_33_out, not_26_out, not_22_out);
  and and_34 (and_34_out, not_26_out, LRU);
  Register #(.width(28)) register_17 (
    .D(CPU_Address[31:4]), .en(and_27_out), .clk(clock1), .Q(register_17_q), .clr(reset));
  Register #(.width(28)) register_18 (
    .D(CPU_Address[31:4]), .en(and_28_out), .clk(clock1), .Q(register_18_q), .clr(reset));
  Register #(.width(28)) register_19 (
    .D(CPU_Address[31:4]), .en(and_29_out), .clk(clock2), .Q(register_19_q), .clr(reset));
  Register #(.width(28)) register_20 (
    .D(CPU_Address[31:4]), .en(and_30_out), .clk(clock2), .Q(register_20_q), .clr(reset));
  Register #(.width(28)) register_21 (
    .D(CPU_Address[31:4]), .en(and_31_out), .clk(clock3), .Q(register_21_q), .clr(reset));
  Register #(.width(28)) register_22 (
    .D(CPU_Address[31:4]), .en(and_32_out), .clk(clock3), .Q(register_22_q), .clr(reset));
  Register #(.width(28)) register_23 (
    .D(CPU_Address[31:4]), .en(and_33_out), .clk(clock4), .Q(register_23_q), .clr(reset));
  Register #(.width(28)) register_24 (
    .D(CPU_Address[31:4]), .en(and_34_out), .clk(clock4), .Q(register_24_q), .clr(reset));
  Comparator #(.mode("unsigned"), .width(28)) comparator_1 (
    .a(register_19_q), .b(CPU_Address[31:4]), .eq(comparator_1_eq));  // open: gt, lt
  Comparator #(.mode("unsigned"), .width(28)) comparator_2 (
    .a(register_20_q), .b(CPU_Address[31:4]), .eq(comparator_2_eq));  // open: gt, lt
  Comparator #(.mode("unsigned"), .width(28)) comparator_3 (
    .a(register_23_q), .b(CPU_Address[31:4]), .eq(comparator_3_eq));  // open: gt, lt
  Comparator #(.mode("unsigned"), .width(28)) comparator_4 (
    .a(register_24_q), .b(CPU_Address[31:4]), .eq(comparator_4_eq));  // open: gt, lt
  Comparator #(.mode("unsigned"), .width(28)) comparator_5 (
    .a(register_17_q), .b(CPU_Address[31:4]), .eq(comparator_5_eq));  // open: gt, lt
  Comparator #(.mode("unsigned"), .width(28)) comparator_6 (
    .a(register_18_q), .b(CPU_Address[31:4]), .eq(comparator_6_eq));  // open: gt, lt
  Comparator #(.mode("unsigned"), .width(28)) comparator_7 (
    .a(register_21_q), .b(CPU_Address[31:4]), .eq(comparator_7_eq));  // open: gt, lt
  Comparator #(.mode("unsigned"), .width(28)) comparator_8 (
    .a(register_22_q), .b(CPU_Address[31:4]), .eq(comparator_8_eq));  // open: gt, lt
  not not_23 (not_23_out, hit1);
  and and_35 (and_35_out, v11, comparator_5_eq);
  and and_36 (and_36_out, v12, comparator_6_eq);
  not not_24 (not_24_out, hit2);
  and and_37 (and_37_out, v21, comparator_1_eq);
  and and_38 (and_38_out, v22, comparator_2_eq);
  not not_25 (not_25_out, hit3);
  and and_39 (and_39_out, v31, comparator_7_eq);
  and and_40 (and_40_out, v32, comparator_8_eq);
  not not_26 (not_26_out, hit4);
  and and_41 (and_41_out, v41, comparator_3_eq);
  and and_42 (and_42_out, v42, comparator_4_eq);
  or or_12 (hit1, and_35_out, and_36_out);
  Multiplexer multiplexer_1 (.in0(LRU), .in1(and_36_out), .out(block_index), .sel(hit1));
  or or_13 (hit2, and_37_out, and_38_out);
  Multiplexer multiplexer_2 (.in0(LRU), .in1(and_38_out), .out(block_index), .sel(hit2));
  or or_14 (hit3, and_39_out, and_40_out);
  Multiplexer multiplexer_3 (.in0(LRU), .in1(and_40_out), .out(block_index), .sel(hit3));
  or or_15 (hit4, and_41_out, and_42_out);
  Multiplexer multiplexer_4 (.in0(LRU), .in1(and_42_out), .out(block_index), .sel(hit4));
  not not_27 (not_27_out, Hit);
  or or_16 (or_16_out, dirty_b12, dirty_b11);
  or or_17 (or_17_out, dirty_b22, dirty_b21);
  or or_18 (or_18_out, dirty_b32, dirty_b31);
  or or_19 (or_19_out, dirty_b42, dirty_b41);
  or or_20 (or_20_out, or_16_out, or_17_out, or_18_out, or_19_out);
  and and_43 (and_43_out, not_27_out, or_20_out);
  Multiplexer #(.width(4)) multiplexer_5 (.in0(MemWriteMask), .in1(4'b1111), .out(writeMask), .sel(and_43_out));

  // Other names for the same wires on the sheet: word_index[1:0] = CPU_Address[1:0];
  //   set_index[1:0] = CPU_Address[3:2]; tag[27:0] = CPU_Address[31:4]; readData[31:0] = raedData

  // Notes on the sheet:
  //   tag: 28 bit, set: 2bit, word: 2bit
  //   inputs
  //   sets seperation
  //   clocks
  //   valid bits
  //   set1
  //   set2
  //   set3
  //   set4
  //   dirty bits
  //   tag array
  //   tag array
  //   tag array
  //   tag array
endmodule
