// Logisim project cacheController.circ as structural Verilog: 1 circuit, main circuit cahceCU
module cahceCU (
  input  [31:0] CPU_Address,
  input  LRU,
  input  CLOCK,
  input  RESET,
  output LRU_out
);

  wire clock1, clock2, clock3, clock4, LRU1, LRU2, LRU3, LRU4, set1, set2, set3, set4;

  and and_1 (clock1, CLOCK, set1);
  Register #(.width(1)) register_1 (.D(LRU), .en(1'b1), .clk(clock1), .Q(LRU1), .clr(RESET));
  and and_2 (clock2, CLOCK, set2);
  Register #(.width(1)) register_2 (.D(LRU), .en(1'b1), .clk(clock2), .Q(LRU2), .clr(RESET));
  and and_3 (clock3, CLOCK, set3);
  Decoder #(.select(2)) decoder_1 (
    .out0(set1), .out1(set2), .out2(set3), .out3(set4), .sel(CPU_Address[29:28]), .en(1'b1));
  and and_4 (clock4, CLOCK, set4);
  Register #(.width(1)) register_3 (.D(LRU), .en(1'b1), .clk(clock3), .Q(LRU3), .clr(RESET));
  Register #(.width(1)) register_4 (.D(LRU), .en(1'b1), .clk(clock4), .Q(LRU4), .clr(RESET));
  Multiplexer #(.select(2)) multiplexer_1 (
    .in0(LRU1), .in1(LRU2), .in2(LRU3), .in3(LRU4), .out(LRU_out), .sel(CPU_Address[29:28]));

  // Other names for the same wires on the sheet: tag[27:0] = CPU_Address[27:0]; set_index[1:0] = CPU_Address[29:28];
  //   word_index[1:0] = CPU_Address[31:30]

  // Notes on the sheet:
  //   tag: 10 bit, set: 2bit, word: 2bit
  //   works: dirty bit/ tag bits/ transfering beetwin m.m and c.m and cpu / LRU
  //   LRU bit
endmodule
