// Logisim project display.circ as structural Verilog: 1 circuit, main circuit main
module main (
  input  [4:0] RegInput,
  output buttomRight1,
  output buttomRight,
  output buttomLeft1,
  output buttomLeft,
  output buttom,
  output middle,
  output middle1,
  output top,
  output top1,
  output topLeft,
  output topLeft1,
  output topRight
);

  wire and_1_out, and_2_out, and_3_out, and_4_out, and_5_out, and_6_out, and_7_out, and_8_out, and_9_out,
       and_10_out, and_11_out, and_12_out, and_13_out, and_14_out, and_15_out, and_16_out, and_17_out,
       and_18_out, and_19_out, and_20_out, and_21_out, and_22_out, and_23_out, and_24_out, and_25_out,
       and_26_out, and_27_out, and_28_out, and_29_out, and_30_out, and_31_out, and_32_out, and_33_out,
       and_34_out, and_35_out, and_36_out, and_37_out, and_38_out, and_39_out, and_40_out, and_41_out,
       and_42_out, and_43_out, and_44_out, and_45_out, and_46_out, and_47_out, and_48_out, and_49_out,
       and_50_out, and_51_out, and_52_out, and_53_out, and_54_out, and_55_out, and_56_out, and_57_out,
       and_58_out, and_59_out, and_60_out, and_61_out, and_62_out, and_63_out, and_64_out, and_65_out,
       and_66_out, and_67_out, not_1_out, not_2_out, not_3_out, not_4_out, not_5_out, not_6_out, not_7_out,
       not_8_out, not_9_out, not_11_out, not_12_out, not_13_out, not_14_out, not_15_out, not_16_out,
       not_17_out, not_18_out, not_19_out;

  not not_1 (not_1_out, RegInput[4]);
  not not_2 (not_2_out, RegInput[3]);
  not not_3 (not_3_out, RegInput[2]);
  not not_4 (not_4_out, RegInput[1]);
  not not_5 (not_5_out, RegInput[0]);
  and and_1 (and_1_out, not_2_out, not_4_out, not_5_out);
  not not_6 (not_6_out, RegInput[4]);
  not not_7 (not_7_out, RegInput[3]);
  not not_8 (not_8_out, RegInput[2]);
  not not_9 (not_9_out, RegInput[1]);
  // NOT_Gate not_10 has open pins: in=RegInput[0], out=open
  not not_11 (not_11_out, RegInput[4]);
  not not_12 (not_12_out, RegInput[3]);
  not not_13 (not_13_out, RegInput[2]);
  not not_14 (not_14_out, RegInput[1]);
  not not_15 (not_15_out, RegInput[4]);
  not not_16 (not_16_out, RegInput[3]);
  not not_17 (not_17_out, RegInput[2]);
  not not_18 (not_18_out, RegInput[1]);
  not not_19 (not_19_out, RegInput[0]);
  and and_2 (and_2_out, not_17_out, not_18_out);
  and and_3 (and_3_out, RegInput[3], not_3_out, not_4_out);
  and and_4 (and_4_out, RegInput[3], RegInput[1], not_5_out);
  and and_5 (and_5_out, not_6_out, not_7_out);
  and and_6 (and_6_out, not_11_out, not_12_out);
  and and_7 (and_7_out, not_12_out, RegInput[2]);
  or or_1 (buttomLeft1, and_6_out, and_7_out, and_15_out, and_14_out, and_20_out);
  and and_8 (and_8_out, RegInput[3], RegInput[1]);
  and and_9 (and_9_out, RegInput[4], not_17_out);
  or or_2 (buttomRight, RegInput[0], and_2_out, and_8_out, and_9_out, and_17_out, and_16_out);
  and and_10 (and_10_out, not_1_out, not_2_out, RegInput[2], not_4_out);
  and and_11 (and_11_out, RegInput[4], RegInput[3], not_4_out);
  or or_3 (topLeft, and_1_out, and_3_out, and_4_out, and_11_out, and_10_out, and_18_out, and_21_out, and_27_out);
  and and_12 (and_12_out, RegInput[4], RegInput[3]);
  and and_13 (and_13_out, not_7_out, RegInput[2]);
  or or_4 (top1, and_5_out, and_13_out, and_12_out, and_19_out);
  and and_14 (and_14_out, RegInput[4], RegInput[2], not_14_out);
  and and_15 (and_15_out, not_11_out, not_13_out, not_14_out);
  and and_16 (and_16_out, not_15_out, not_16_out, RegInput[2]);
  and and_17 (and_17_out, RegInput[4], not_18_out);
  and and_18 (and_18_out, not_1_out, not_2_out, RegInput[2], not_5_out);
  and and_19 (and_19_out, not_6_out, not_8_out, not_9_out);
  and and_20 (and_20_out, RegInput[4], RegInput[3], not_13_out);
  and and_21 (and_21_out, not_1_out, RegInput[3], RegInput[2], RegInput[1]);
  and and_22 (and_22_out, RegInput[4], RegInput[2]);
  and and_23 (and_23_out, RegInput[4], RegInput[3]);
  or or_5 (middle1, and_22_out, and_23_out);
  and and_24 (and_24_out, not_12_out, not_13_out);
  and and_25 (and_25_out, RegInput[3], RegInput[2], RegInput[1]);
  or or_6 (buttomRight1, and_24_out, and_25_out, not_11_out);
  and and_26 (and_26_out, not_15_out, not_17_out, not_19_out);
  and and_27 (and_27_out, RegInput[4], not_2_out, not_3_out, RegInput[1]);
  and and_28 (and_28_out, not_6_out, not_7_out);
  and and_29 (and_29_out, not_6_out, not_8_out, not_9_out);
  or or_7 (topLeft1, and_28_out, and_29_out);
  and and_30 (and_30_out, not_16_out, not_17_out, RegInput[1]);
  and and_31 (and_31_out, not_16_out, RegInput[1], not_19_out);
  and and_32 (and_32_out, not_2_out, RegInput[1]);
  and and_33 (and_33_out, not_1_out, not_3_out, not_5_out);
  and and_34 (and_34_out, RegInput[3], not_18_out, RegInput[0]);
  and and_35 (and_35_out, RegInput[3], RegInput[2], not_18_out);
  or or_8 (buttom, and_45_out, and_26_out, and_30_out, and_31_out, and_34_out, and_35_out, and_38_out, and_39_out, and_42_out, and_46_out);
  and and_36 (and_36_out, not_1_out, RegInput[2], RegInput[0]);
  and and_37 (and_37_out, not_1_out, RegInput[3], not_4_out);
  or or_9 (top, and_32_out, and_33_out, and_36_out, and_37_out, and_40_out, and_41_out, and_43_out, and_44_out);
  and and_38 (and_38_out, RegInput[4], not_16_out, not_19_out);
  and and_39 (and_39_out, RegInput[4], not_16_out, RegInput[1]);
  and and_40 (and_40_out, RegInput[3], RegInput[2], not_4_out);
  and and_41 (and_41_out, RegInput[4], not_2_out, not_5_out);
  and and_42 (and_42_out, RegInput[4], RegInput[1], not_19_out);
  and and_43 (and_43_out, RegInput[4], not_3_out, RegInput[0]);
  and and_44 (and_44_out, RegInput[4], RegInput[1], not_5_out);
  and and_45 (and_45_out, not_15_out, RegInput[2], not_18_out, RegInput[0]);
  and and_46 (and_46_out, not_15_out, RegInput[3], RegInput[2], RegInput[0]);
  and and_47 (and_47_out, RegInput[4], RegInput[2]);
  and and_48 (and_48_out, not_1_out, not_4_out, not_5_out);
  and and_49 (and_49_out, not_16_out, not_17_out, not_19_out);
  and and_50 (and_50_out, not_2_out, not_3_out, RegInput[0]);
  and and_51 (and_51_out, not_2_out, not_3_out, RegInput[1]);
  and and_52 (and_52_out, not_16_out, RegInput[1], not_19_out);
  and and_53 (and_53_out, not_17_out, RegInput[1], not_19_out);
  or or_10 (buttomLeft, and_49_out, and_52_out, and_53_out, and_56_out, and_57_out);
  and and_54 (and_54_out, not_2_out, RegInput[1], RegInput[0]);
  and and_55 (and_55_out, not_3_out, RegInput[1], RegInput[0]);
  or or_11 (topRight, and_47_out, and_48_out, and_50_out, and_51_out, and_60_out, and_54_out, and_55_out, and_58_out, and_59_out);
  and and_56 (and_56_out, RegInput[4], RegInput[2], not_19_out);
  and and_57 (and_57_out, not_15_out, RegInput[3], not_18_out, not_19_out);
  and and_58 (and_58_out, not_1_out, RegInput[3], not_4_out);
  and and_59 (and_59_out, not_1_out, RegInput[3], not_5_out);
  and and_60 (and_60_out, RegInput[3], not_4_out, not_5_out);
  and and_61 (and_61_out, RegInput[3], not_4_out);
  and and_62 (and_62_out, not_2_out, not_3_out, RegInput[1]);
  and and_63 (and_63_out, not_2_out, RegInput[1], not_5_out);
  and and_64 (and_64_out, not_1_out, RegInput[2], not_4_out);
  and and_65 (and_65_out, not_1_out, RegInput[3], RegInput[2]);
  and and_66 (and_66_out, RegInput[4], not_3_out, not_5_out);
  or or_12 (middle, and_62_out, and_63_out, and_64_out, and_61_out, and_65_out, and_66_out, and_67_out);
  and and_67 (and_67_out, RegInput[4], not_2_out, RegInput[1]);

  // Other names for the same wires on the sheet: E = RegInput[0]; fiveBitInp[4:0] = RegInput; D = RegInput[1];
  //   C = RegInput[2]; B = RegInput[3]; A = RegInput[4]
endmodule
