// Logisim project get_biggest.circ as structural Verilog: 1 circuit, main circuit get_biggest
module get_biggest (
  input  [7:0] in_1,
  input  [7:0] in_2,
  input  [7:0] in_3,
  input  [7:0] in_4,
  input  [7:0] in_5,
  input  [7:0] in_6,
  input  [7:0] in_7,
  input  [7:0] in_8,
  output [7:0] out_9
);

  wire comparator_1_lt, comparator_2_lt, comparator_3_lt, comparator_4_lt, comparator_5_lt, comparator_6_lt,
       comparator_7_lt;
  wire [7:0] multiplexer_1_out, multiplexer_2_out, multiplexer_3_out, multiplexer_4_out, multiplexer_5_out,
       multiplexer_6_out;

  Comparator comparator_1 (.a(in_1), .b(in_2), .lt(comparator_1_lt));  // open: gt, eq
  Multiplexer #(.width(8)) multiplexer_1 (.in0(in_1), .in1(in_2), .out(multiplexer_1_out), .sel(comparator_1_lt));
  Comparator comparator_2 (.a(multiplexer_1_out), .b(in_3), .lt(comparator_2_lt));  // open: gt, eq
  Multiplexer #(.width(8)) multiplexer_2 (
    .in0(multiplexer_1_out), .in1(in_3), .out(multiplexer_2_out), .sel(comparator_2_lt));
  Comparator comparator_3 (.a(multiplexer_2_out), .b(in_4), .lt(comparator_3_lt));  // open: gt, eq
  Multiplexer #(.width(8)) multiplexer_3 (
    .in0(multiplexer_2_out), .in1(in_4), .out(multiplexer_3_out), .sel(comparator_3_lt));
  Multiplexer #(.width(8)) multiplexer_4 (
    .in0(multiplexer_3_out), .in1(in_5), .out(multiplexer_4_out), .sel(comparator_4_lt));
  Comparator comparator_4 (.a(multiplexer_3_out), .b(in_5), .lt(comparator_4_lt));  // open: gt, eq
  Comparator comparator_5 (.a(multiplexer_4_out), .b(in_6), .lt(comparator_5_lt));  // open: gt, eq
  Multiplexer #(.width(8)) multiplexer_5 (
    .in0(multiplexer_4_out), .in1(in_6), .out(multiplexer_5_out), .sel(comparator_5_lt));
  Multiplexer #(.width(8)) multiplexer_6 (
    .in0(multiplexer_5_out), .in1(in_7), .out(multiplexer_6_out), .sel(comparator_6_lt));
  Comparator comparator_6 (.a(multiplexer_5_out), .b(in_7), .lt(comparator_6_lt));  // open: gt, eq
  Multiplexer #(.width(8)) multiplexer_7 (.in0(multiplexer_6_out), .in1(in_8), .out(out_9), .sel(comparator_7_lt));
  Comparator comparator_7 (.a(multiplexer_6_out), .b(in_8), .lt(comparator_7_lt));  // open: gt, eq

  // Other names for the same wires on the sheet: c1[7:0] = in_1; c2[7:0] = in_2; c3[7:0] = in_3; c4[7:0] = in_4;
  //   c5[7:0] = in_5; c6[7:0] = in_6; c7[7:0] = in_7; c8[7:0] = in_8
endmodule
