// Logisim project instruction_splitter.circ as structural Verilog: 1 circuit, main circuit instruction_splitter
module instruction_splitter (
  input  [31:0] instruction,
  output [5:0] op,
  output [25:0] target26,
  output [4:0] rs,
  output [4:0] rt,
  output [15:0] imm16,
  output [4:0] rd,
  output [4:0] shamt,
  output [5:0] func
);


  assign func = instruction[5:0];
  assign imm16 = instruction[15:0];
  assign op = instruction[31:26];
  assign rd = instruction[15:11];
  assign rs = instruction[25:21];
  assign rt = instruction[20:16];
  assign shamt = instruction[10:6];
  assign target26 = instruction[25:0];

  // Notes on the sheet:
  //   j-format
endmodule
