// Logisim project mux2x32.circ as structural Verilog: 1 circuit, main circuit mux2x32
module mux2x32 (
  input  [31:0] x0,
  input  [31:0] x1,
  input  Sel,
  output [31:0] Y
);

  Multiplexer #(.width(32)) multiplexer_1 (.in0(x0), .in1(x1), .out(Y), .sel(Sel));
endmodule
