// Logisim project mux2x5.circ as structural Verilog: 1 circuit, main circuit mux2x5
module mux2x5 (
  input  [4:0] X0,
  input  [4:0] X1,
  input  Sel,
  output [4:0] Y
);

  MUX2x1 mux2x1_1 (.X0(X0[0]), .X1(X1[0]), .Sel(Sel), .Y(Y[0]));
  MUX2x1 mux2x1_2 (.X0(X0[1]), .X1(X1[3]), .Sel(Sel), .Y(Y[1]));
  MUX2x1 mux2x1_3 (.X0(X0[2]), .X1(X1[3]), .Sel(Sel), .Y(Y[2]));
  MUX2x1 mux2x1_4 (.X0(X0[3]), .X1(X1[3]), .Sel(Sel), .Y(Y[3]));
  MUX2x1 mux2x1_5 (.X0(X0[4]), .X1(X1[4]), .Sel(Sel), .Y(Y[4]));

  assign X1[2:1] = {2{X1[3]}};
endmodule
