// Logisim project set.circ as structural Verilog: 1 circuit, main circuit set
module set (
  input  [31:0] data_in,
  input  [1:0] word_index,
  input  block_index,
  input  [3:0] MemWriteMask,
  input  CLOCK,
  input  RESET,
  output [31:0] MemReadData
);

  wire and_1_out, and_2_out, not_1_out;

  and and_1 (and_1_out, CLOCK, not_1_out);
  not not_1 (not_1_out, block_index);
  and and_2 (and_2_out, CLOCK, block_index);
  B_lock b_lock_1 (
    .data_in(data_in), .word_index(word_index), .MemWriteMask(MemWriteMask), .CLOCK(and_1_out),
    .RESET(RESET), .readData(MemReadData));
  B_lock b_lock_2 (
    .data_in(data_in), .word_index(word_index), .MemWriteMask(MemWriteMask), .CLOCK(and_2_out),
    .RESET(RESET), .readData(MemReadData));
endmodule
